// Logisim project projeto1.circ as structural Verilog: 5 circuits, main circuit AND
module AND (
  input  A,
  input  B,
  output out_3
);

  wire or_1_out;

  or or_1 (or_1_out, ~A, ~B);  // OR_Gate
  not not_1 (out_3, or_1_out);
endmodule

module OR (
  input  A,
  input  B,
  output out_3
);

  wire and_1_out;

  and and_1 (and_1_out, ~A, ~B);  // AND_Gate
  not not_1 (out_3, and_1_out);
endmodule

// T
module q2 (
  input  A,
  input  B,
  input  C,
  output T,
  output S
);

  wire and_1_out, and_2_out, and_3_out, and_4_out, and_5_out, and_6_out, and_7_out;

  and and_1 (and_1_out, A, B);
  and and_2 (and_2_out, A, C);
  and and_3 (and_3_out, B, C);
  and and_4 (and_4_out, ~A, ~B, C);  // AND_Gate
  and and_5 (and_5_out, ~A, B, ~C);  // AND_Gate
  and and_6 (and_6_out, A, ~B, ~C);  // AND_Gate
  and and_7 (and_7_out, A, B, C);
  or or_1 (T, and_1_out, and_2_out, and_3_out);
  or or_2 (S, and_4_out, and_5_out, and_6_out, and_7_out);
endmodule

module q3 (
  input  A,
  input  B,
  input  C,
  output T,
  output S
);

  wire nand_1_out, nand_2_out, nand_3_out, nand_4_out, nand_5_out, nand_6_out, nand_7_out;

  nand nand_1 (nand_1_out, A, B);
  nand nand_2 (nand_2_out, A, C);
  nand nand_3 (nand_3_out, B, C);
  nand nand_4 (nand_4_out, ~A, ~B, C);  // NAND_Gate
  nand nand_5 (nand_5_out, ~A, B, ~C);  // NAND_Gate
  nand nand_6 (nand_6_out, A, ~B, ~C);  // NAND_Gate
  nand nand_7 (nand_7_out, A, B, C);
  nand nand_8 (T, nand_1_out, nand_2_out, nand_3_out);
  nand nand_9 (S, nand_4_out, nand_5_out, nand_6_out, nand_7_out);
endmodule

module q4 (
  input  S1,
  input  S0,
  input  D0,
  input  D1,
  input  D2,
  input  D3,
  output Y
);

  wire nand_1_out, nand_2_out, nand_3_out, nand_4_out;

  nand nand_1 (nand_1_out, ~S1, ~S0, D0);  // NAND_Gate
  nand nand_2 (nand_2_out, ~S1, S0, D1);  // NAND_Gate
  nand nand_3 (nand_3_out, S1, ~S0, D2);  // NAND_Gate
  nand nand_4 (nand_4_out, S1, S0, D3);
  nand nand_5 (Y, nand_1_out, nand_2_out, nand_3_out, nand_4_out);
endmodule
